# Fritzing sketch main (saved by Fritzing 0.9.10b)
breadboards: 1

parts:
  DHT11_1 = DHT11 module
  WeMos_D1_R1 = WeMos D1 R2
  Mod1 = KY-019 5V Relay Module [package="Breakout board"]
  J1 = Piezo Speaker
  Q1 = Basic FET P-Channel [package="TO220 [THT]"]
  Q2 = Basic FET N-Channel [package="TO220 [THT]"]
  Q3 = Basic FET N-Channel [package="TO220 [THT]"]
  LED2 = RGB LED (com. cathode, rgb) [package="5 mm [THT]"]
  WATER_PUMP1 = water pump/motor  # not connected

nets:
  VCC: DHT11_1.VCC, WeMos_D1_R1.5V, Mod1.+, Mod1.Common, LED2.red_anode
  GND: DHT11_1.GND, WeMos_D1_R1.GND, Mod1.-, J1.pin1, Q1.source, Q2.source, Q3.source
  N1: DHT11_1.DATA, WeMos_D1_R1.D1/TX
  N2: WeMos_D1_R1.(D6), Mod1.S
  N3: WeMos_D1_R1.D8, Q3.gate
  N4: WeMos_D1_R1.D9, Q2.gate
  N5: WeMos_D1_R1.D10, Q1.gate
  N6: Mod1.NO, J1.pin2
  N7: Q1.drain, LED2.blue_anode
  N8: Q2.drain, LED2.green_anode
  N9: Q3.drain, LED2.common_cathode

custom parts:
  DHT11 module: https://cdn-learn.adafruit.com/downloads/pdf/dht.pdf DHT11 black pcb module reference by:https://github.com/adafruit/Fritzing-Library/blob/master/parts/DHT11%20Humitidy%20and%20Temperature%20Sensor.fzpz
  WeMos D1 R2: The D1 R2 is a mini wifi board based on the ESP-8266EX.
  KY-019 5V Relay Module: KY-019 5V Relay module, used to control AC circuits. (Special thanks to vanepp for fixing the PCB holes and other errors)
  RGB LED (com. cathode, rgb): A 5mm tri-color LED with red, green and blue inside.
  water pump/motor: WATER PUMP BY ARDUBLOCKTR
